# Fritzing sketch connect (saved by Fritzing 0.9.2b)

parts:
  Raspberry_Pi = Raspberry Pi 2
  RGB_LED = Super Flux RGB LED (com. anode)

nets:
  N1: Raspberry_Pi.GPIO18, RGB_LED.green_cathode
  N2: Raspberry_Pi.GPIO15, RGB_LED.red_cathode
  N3: Raspberry_Pi.GPIO14, RGB_LED.blue_cathode
  N4: Raspberry_Pi.5V, RGB_LED.common_anode
